# Fritzing sketch circuito_aurora (saved by Fritzing 0.9.3b)
breadboards: 2

parts:
  Componente3 = Arduino Mega ADK (Rev3)
  Componente4 = Arduino Mega ADK (Rev3)
  U1 = 7-SEGMENT-4DIGIT [package=7-segment-4digit-youngsun]
  J1 = Piezo Speaker
  LED1 = RGB LED - (4 legs) [package="5 mm [THT]"]
  Componente5 = RFID USB Reader
  U3 = LCD-16X2 [package=lcd-16x2]
  J2 = Basic Servo
  R1 = Photocell (LDR) [package=THT]
  R3 = Resistor [tolerance=±5% resistance=220 package="1206 [SMD]"]
  R4 = Resistor [tolerance=±5% resistance=220 package="1206 [SMD]"]
  R5 = Resistor [tolerance=±5% resistance=220 package="1206 [SMD]"]
  U4 = POT [package=pot_mammoth]
  R6 = Resistor [tolerance=±5% resistance=220 package="1206 [SMD]"]
  R7 = Resistor [tolerance=±5% resistance=220 package="1206 [SMD]"]

nets:
  N1: Componente3.GND, J1.pin1, LED1.common_anode
  N2: Componente3.D8_PWM, R5.Pin_1
  N3: Componente3.D2_PWM, R4.Pin_1
  N4: Componente3.D3_PWM, R3.Pin_1
  N5: Componente3.D4_PWM, R6.Pin_1
  N6: Componente3.D30, U1.1
  N7: Componente3.D31, U1.16
  N8: Componente3.D32, U1.2
  N9: Componente3.D33, U1.15
  N10: Componente3.D34, U1.3
  N11: Componente3.D35, U1.14
  N12: Componente3.D36, U1.4
  N13: Componente3.D37, U1.13
  N14: Componente3.D38, U1.5
  N15: Componente3.D40, U1.6
  N16: Componente3.D41, U1.11
  N17: Componente4.A8, R1.pin_1, R7.Pin_1
  3V3: Componente4.3V3, Componente5.VCC
  5V: Componente4.5V, U3.VDD, U3.A, J2.vcc, R1.pin_0, U4.E
  GND: Componente4.GND, Componente5.TX-O, U3.VSS, U3.R_W, J2.gnd, U4.S, R7.Pin_0
  N18: Componente4.D7_PWM, J2.pulse
  N19: Componente4.D31, U3.DB7
  N20: Componente4.D33, U3.DB6
  N21: Componente4.D35, U3.DB5
  N22: Componente4.D37, U3.DB4
  N23: Componente4.D39, U3.E
  N24: Componente4.D41, U3.RS
  N25: Componente4.D49, Componente5.GND
  N26: Componente4.D50/MISO, Componente5.ANT1
  N27: Componente4.D51/MOSI, Componente5.ANT2
  N28: Componente4.D52/SCK, Componente5.CP
  N29: Componente4.D53/SS, Componente5.GNDT
  N30: J1.pin2, R5.Pin_0
  N31: LED1.red_cathode, R6.Pin_0
  N32: LED1.green_cathode, R3.Pin_0
  N33: LED1.blue_cathode, R4.Pin_0
  N34: U3.VO, U4.A
